# Fritzing sketch A6(Fritzing) (saved by Fritzing 0.9.3b)
breadboards: 1

parts:
  Arduino = Arduino Uno (Rev3)
  LED1 = smd LED [color="Red (633nm)" package="1206 [SMD]"]
  LED2 = smd LED [color="Red (633nm)" package="1206 [SMD]"]
  LED3 = smd LED [color="Red (633nm)" package="1206 [SMD]"]
  LED4 = smd LED [color="Red (633nm)" package="1206 [SMD]"]
  LED5 = smd LED [color="Red (633nm)" package="1206 [SMD]"]
  LED6 = smd LED [color="Red (633nm)" package="1206 [SMD]"]
  LED7 = smd LED [color="Red (633nm)" package="1206 [SMD]"]
  LED8 = smd LED [color="Red (633nm)" package="1206 [SMD]"]
  LED9 = smd LED [color="Red (633nm)" package="1206 [SMD]"]
  LED10 = smd LED [color="Red (633nm)" package="1206 [SMD]"]
  SG3 = Buzzer 12mm [package=buzzer-12mm-ns]
  S2 = Pushbutton [package="[SMD]"]
  R1 = Resistor [tolerance=±5% resistance=10k package=THT]
  R2 = Resistor [tolerance=±5% resistance=330 package=THT]
  Componente1 = HC-06

nets:
  N1: Arduino.D8, SG3.1
  N2: Arduino.D2, Componente1.connector12
  N3: Arduino.D3_PWM, Componente1.connector13
  N4: Arduino.D5_PWM, LED1.anode, LED2.anode, LED3.anode, LED4.anode, LED5.anode, LED6.anode, LED7.anode, LED8.anode, LED9.anode, LED10.anode
  N5: Arduino.D6_PWM, S2.Pin_1, S2.Pin_2, R1.Pin_0
  N6: Arduino.5V, R1.Pin_1, Componente1.connector15
  N7: Arduino.GND, SG3.2, S2.Pin_3, S2.Pin_4, R2.Pin_1, Componente1.connector14
  N8: LED1.cathode, LED2.cathode, LED3.cathode, LED4.cathode, LED5.cathode, LED6.cathode, LED7.cathode, LED8.cathode, LED9.cathode, LED10.cathode, R2.Pin_0
